// Logisim project RISC_V.circ as structural Verilog
module main (
  input  x,
  input  y,
  output s,
  output carry_out
);

  and and_1 (carry_out, x, y);
  xor xor_1 (s, x, x);
endmodule

module full_adder (
  input  x,
  input  y,
  input  carry_in,
  output s,
  output carry_out
);

  wire half_adder_1_carry_out, half_adder_1_s, half_adder_2_carry_out;

  half_adder half_adder_1 (.x(x), .y(y), .s(half_adder_1_s), .carry_out(half_adder_1_carry_out));
  half_adder half_adder_2 (.x(half_adder_1_s), .y(carry_in), .s(s), .carry_out(half_adder_2_carry_out));
  or or_1 (carry_out, half_adder_2_carry_out, half_adder_1_carry_out);
endmodule

module half_adder (
  input  x,
  input  y,
  output s,
  output carry_out
);

  xor xor_1 (s, x, y);
  and and_1 (carry_out, x, y);
endmodule

module adder_8bit (
  input  [7:0] x,
  input  [7:0] y,
  input  carry_in,
  output c_out,
  output [7:0] s
);

  wire c_0, c_1, c_2, c_3, c_4, c_5, c_6;

  full_adder full_adder_1 (.x(x[7]), .y(y[7]), .carry_in(c_6), .s(s[7]), .carry_out(c_out));
  full_adder full_adder_2 (.x(x[6]), .y(y[6]), .carry_in(c_5), .s(s[6]), .carry_out(c_6));
  full_adder full_adder_3 (.x(x[5]), .y(y[5]), .carry_in(c_4), .s(s[5]), .carry_out(c_5));
  full_adder full_adder_4 (.x(x[4]), .y(y[4]), .carry_in(c_3), .s(s[4]), .carry_out(c_4));
  full_adder full_adder_5 (.x(x[3]), .y(y[3]), .carry_in(c_2), .s(s[3]), .carry_out(c_3));
  full_adder full_adder_6 (.x(x[2]), .y(y[2]), .carry_in(c_1), .s(s[2]), .carry_out(c_2));
  full_adder full_adder_7 (.x(x[1]), .y(y[1]), .carry_in(c_0), .s(s[1]), .carry_out(c_1));
  full_adder full_adder_8 (.x(x[0]), .y(y[0]), .carry_in(carry_in), .s(s[0]), .carry_out(c_0));

  // Other names for the same wires on the sheet: in_0 = carry_in; ovf = c_out; s_0 = s[0]; s_1 = s[1]; s_2 = s[2];
  //   s_3 = s[3]; s_4 = s[4]; s_5 = s[5]; s_6 = s[6]; s_7 = s[7]; x_0 = x[0]; x_1 = x[1]; x_2 = x[2]; x_3 = x[3];
  //   x_4 = x[4]; x_5 = x[5]; x_6 = x[6]; x_7 = x[7]; y_0 = y[0]; y_1 = y[1]; y_2 = y[2]; y_3 = y[3]; y_4 = y[4];
  //   y_5 = y[5]; y_6 = y[6]; y_7 = y[7]
endmodule

module adder_32bit (
  input  carry_in,
  input  [31:0] y,
  input  [31:0] x,
  output c_out,
  output [31:0] s
);

  wire c_0, c_1, c_2;

  adder_8bit adder_8bit_1 (.x(x[31:24]), .y(y[31:24]), .carry_in(c_2), .c_out(c_out), .s(s[31:24]));
  adder_8bit adder_8bit_2 (.x(x[23:16]), .y(y[23:16]), .carry_in(c_1), .c_out(c_2), .s(s[23:16]));
  adder_8bit adder_8bit_3 (.x(x[15:8]), .y(y[15:8]), .carry_in(c_0), .c_out(c_1), .s(s[15:8]));
  adder_8bit adder_8bit_4 (.x(x[7:0]), .y(y[7:0]), .carry_in(carry_in), .c_out(c_0), .s(s[7:0]));

  // Other names for the same wires on the sheet: in_0 = carry_in; ovf = c_out; s_0[7:0] = s[7:0]; s_1[7:0] = s[15:8];
  //   s_2[7:0] = s[23:16]; s_3[7:0] = s[31:24]; x_0[7:0] = x[7:0]; x_1[7:0] = x[15:8]; x_2[7:0] = x[23:16];
  //   x_3[7:0] = x[31:24]; y_0[7:0] = y[7:0]; y_1[7:0] = y[15:8]; y_2[7:0] = y[23:16]; y_3[7:0] = y[31:24]
endmodule

module word_inverter (
  input  [31:0] a,
  output [31:0] y
);

  byte_inverter byte_inverter_1 (.a(a[31:24]), .y(y[31:24]));
  byte_inverter byte_inverter_2 (.a(a[23:16]), .y(y[23:16]));
  byte_inverter byte_inverter_3 (.a(a[15:8]), .y(y[15:8]));
  byte_inverter byte_inverter_4 (.a(a[7:0]), .y(y[7:0]));

  // Other names for the same wires on the sheet: a_0[7:0] = a[7:0]; a_1[7:0] = a[15:8]; a_2[7:0] = a[23:16];
  //   a_3[7:0] = a[31:24]; y_0[7:0] = y[7:0]; y_1[7:0] = y[15:8]; y_2[7:0] = y[23:16]; y_3[7:0] = y[31:24]
endmodule

module byte_inverter (
  input  [7:0] a,
  output [7:0] y
);

  not not_1 (y[0], a[0]);
  not not_2 (y[1], a[1]);
  not not_3 (y[2], a[2]);
  not not_4 (y[3], a[3]);
  not not_5 (y[4], a[4]);
  not not_6 (y[5], a[5]);
  not not_7 (y[6], a[6]);
  not not_8 (y[7], a[7]);
endmodule

module ALU (
  input  [31:0] a,
  input  [31:0] b,
  input  [2:0] sel,
  output [31:0] y,
  output carry
);

  wire and_1_out, not_1_out, xnor_1_out, xor_1_out, xor_2_out;
  wire [31:0] ls, s, s_and, s_or, s_xor;

  NotExactlyOne xnor_1 (.out(xnor_1_out), .in0(b[31]), .in1(sel[0]), .in2(a[31]));
  not not_1 (not_1_out, sel[1]);
  xor xor_1 (xor_1_out, s[31], a[31]);
  and and_1 (and_1_out, xnor_1_out, not_1_out, xor_1_out);
  xor xor_2 (xor_2_out, and_1_out, s[31]);
  Arithmetic_engine arithmetic_engine_1 (.sel(sel[0]), .a(a), .b(b), .carry(carry), .s(s));
  Logic_engine logic_engine_1 (.a(a), .b(b), .s(s_and), .s_or(s_or), .s_xor(s_xor));
  zero_extender zero_extender_1 (.a(xor_2_out), .q(ls));
  Multiplexer #(.select(3), .width(32)) multiplexer_1 (
    .in0(s), .in1(s), .in2(s_and), .in3(s_or), .in4(s_xor), .in5(ls), .out(y), .sel(sel));  // open: in6, in7

  // Other names for the same wires on the sheet: x[31:0] = a; x31 = a[31]; y_t[31:0] = b; y31 = b[31]; op[2:0] = sel;
  //   sel_t = sel[0]; sel_1 = sel[1]; q[31:0] = y
endmodule

module and_byte (
  input  [7:0] a,
  input  [7:0] b,
  output [7:0] y
);

  and and_1 (y[0], a[0], b[0]);
  and and_2 (y[1], a[1], b[1]);
  and and_3 (y[2], a[2], b[2]);
  and and_4 (y[3], a[3], b[3]);
  and and_5 (y[4], a[4], b[4]);
  and and_6 (y[5], a[5], b[5]);
  and and_7 (y[6], a[6], b[6]);
  and and_8 (y[7], a[7], b[7]);
endmodule

module or_byte (
  input  [7:0] a,
  input  [7:0] b,
  output [7:0] y
);

  or or_1 (y[0], a[0], b[0]);
  or or_2 (y[1], a[1], b[1]);
  or or_3 (y[2], a[2], b[2]);
  or or_4 (y[3], a[3], b[3]);
  or or_5 (y[4], a[4], b[4]);
  or or_6 (y[5], a[5], b[5]);
  or or_7 (y[6], a[6], b[6]);
  or or_8 (y[7], a[7], b[7]);
endmodule

module and_word (
  input  [31:0] a,
  input  [31:0] b,
  output [31:0] s
);

  and_byte and_byte_1 (.a(a[31:24]), .b(b[31:24]), .y(s[31:24]));
  and_byte and_byte_2 (.a(a[23:16]), .b(b[23:16]), .y(s[23:16]));
  and_byte and_byte_3 (.a(a[15:8]), .b(b[15:8]), .y(s[15:8]));
  and_byte and_byte_4 (.a(a[7:0]), .b(b[7:0]), .y(s[7:0]));

  // Other names for the same wires on the sheet: a_0[7:0] = a[7:0]; a_1[7:0] = a[15:8]; a_2[7:0] = a[23:16];
  //   a_3[7:0] = a[31:24]; b_0[7:0] = b[7:0]; b_1[7:0] = b[15:8]; b_2[7:0] = b[23:16]; b_3[7:0] = b[31:24];
  //   s_0[7:0] = s[7:0]; s_1[7:0] = s[15:8]; s_2[7:0] = s[23:16]; s_3[7:0] = s[31:24]
endmodule

module or_word (
  input  [31:0] a,
  input  [31:0] b,
  output [31:0] s
);

  or_byte or_byte_1 (.a(a[31:24]), .b(b[31:24]), .y(s[31:24]));
  or_byte or_byte_2 (.a(a[23:16]), .b(b[23:16]), .y(s[23:16]));
  or_byte or_byte_3 (.a(a[15:8]), .b(b[15:8]), .y(s[15:8]));
  or_byte or_byte_4 (.a(a[7:0]), .b(b[7:0]), .y(s[7:0]));

  // Other names for the same wires on the sheet: a_0[7:0] = a[7:0]; a_1[7:0] = a[15:8]; a_2[7:0] = a[23:16];
  //   a_3[7:0] = a[31:24]; b_0[7:0] = b[7:0]; b_1[7:0] = b[15:8]; b_2[7:0] = b[23:16]; b_3[7:0] = b[31:24];
  //   s_0[7:0] = s[7:0]; s_1[7:0] = s[15:8]; s_2[7:0] = s[23:16]; s_3[7:0] = s[31:24]
endmodule

module ALU_test (
  input  [1:0] sel,
  input  [31:0] a,
  input  [31:0] b,
  output overflow,
  output carry_out,
  output [31:0] y
);

  // ALU alu_1: pin names not known

  // Other names for the same wires on the sheet: carry = carry_out; ovf = overflow
endmodule

module zero_extender (
  input  a,
  output [31:0] q
);

  or or_1 (q[0], a, 1'b0);

  assign q[31:1] = {31{1'b0}};
endmodule

module Arithmetic_engine (
  input  sel,
  input  [31:0] a,
  input  [31:0] b,
  output carry,
  output [31:0] s
);

  wire [31:0] multiplexer_1_out, word_inverter_1_y;

  word_inverter word_inverter_1 (.a(b), .y(word_inverter_1_y));
  Multiplexer #(.width(32)) multiplexer_1 (.in0(b), .in1(word_inverter_1_y), .out(multiplexer_1_out), .sel(sel));
  adder_32bit adder_32bit_1 (.carry_in(sel), .y(a), .x(multiplexer_1_out), .c_out(carry), .s(s));

  // Other names for the same wires on the sheet: x[31:0] = a; y[31:0] = b
endmodule

module Logic_engine (
  input  [31:0] a,
  input  [31:0] b,
  output [31:0] s,
  output [31:0] s_or,
  output [31:0] s_xor
);

  xor_word xor_word_1 (.a(a), .b(b), .s(s_xor));
  or_word or_word_1 (.a(a), .b(b), .s(s_or));
  and_word and_word_1 (.a(a), .b(b), .s(s));

  // Other names for the same wires on the sheet: x[31:0] = a; y[31:0] = b; s_and[31:0] = s
endmodule

module xor_byte (
  input  [7:0] a,
  input  [7:0] b,
  output [7:0] y
);

  xor xor_1 (y[0], a[0], b[0]);
  xor xor_2 (y[1], a[1], b[1]);
  xor xor_3 (y[2], a[2], b[2]);
  xor xor_4 (y[3], a[3], b[3]);
  xor xor_5 (y[4], a[4], b[4]);
  xor xor_6 (y[5], a[5], b[5]);
  xor xor_7 (y[6], a[6], b[6]);
  xor xor_8 (y[7], a[7], b[7]);
endmodule

module xor_word (
  input  [31:0] a,
  input  [31:0] b,
  output [31:0] s
);

  xor_byte xor_byte_1 (.a(a[31:24]), .b(b[31:24]), .y(s[31:24]));
  xor_byte xor_byte_2 (.a(a[23:16]), .b(b[23:16]), .y(s[23:16]));
  xor_byte xor_byte_3 (.a(a[15:8]), .b(b[15:8]), .y(s[15:8]));
  xor_byte xor_byte_4 (.a(a[7:0]), .b(b[7:0]), .y(s[7:0]));

  // Other names for the same wires on the sheet: a_0[7:0] = a[7:0]; a_1[7:0] = a[15:8]; a_2[7:0] = a[23:16];
  //   a_3[7:0] = a[31:24]; b_0[7:0] = b[7:0]; b_1[7:0] = b[15:8]; b_2[7:0] = b[23:16]; b_3[7:0] = b[31:24];
  //   s_0[7:0] = s[7:0]; s_1[7:0] = s[15:8]; s_2[7:0] = s[23:16]; s_3[7:0] = s[31:24]
endmodule

module data_memory (
);

  RAM #(.\type ("nonvolatile")) ram_1 ();  // open: addr, we, oe, clk, din, dout
endmodule
